# Fritzing sketch ultrasonic sensor sketch (saved by Fritzing 0.8.7b)
breadboards: 1

parts:
  Part1 = Arduino Uno (Rev3)
  Part2 = SRF05 Ultrasonic Rangefinder

nets:
  GND: Part1.GND, Part2.GND
  N1: Part1.D2, Part2.Trig
  N2: Part1.D3_PWM, Part2.Echo
  5V: Part1.5V, Part2.VCC
